// Logisim project log.circ as structural Verilog: 6 circuits, main circuit motherboard
module motherboard (
);

  wire clock_1_out;
  wire [1:0] cpu_1_ramctrl;
  wire [7:0] ram_1_data;
  wire [15:0] cpu_1_ramout;

  CPU cpu_1 (.ClkIn(clock_1_out), .RAMOut(cpu_1_ramout), .RAMCtrl(cpu_1_ramctrl), .RAMIn(ram_1_data));
  Clock clock_1 (.out(clock_1_out));
  // Probe on cpu_1_ramout
  // Probe on ram_1_data
  RAM #(.addrWidth(16)) ram_1 (
    .addr(cpu_1_ramout), .data(ram_1_data), .clk(cpu_1_ramctrl[1]), .ld(cpu_1_ramctrl[0]));  // open: sel, clr
  TTY tty_1 ();  // open: data, clk, we, clr
endmodule

module CPU (
  input  [7:0] RAMIn,
  input  ClkIn,
  output [15:0] RAMOut,
  output [1:0] RAMCtrl
);

  wire decoder_1_out0, decoder_1_out1, decoder_1_out2, decoder_1_out3, not_1_out, or_1_out;
  wire [1:0] flg_1_out_3, regdec_1_out_4, regdec_1_out_4_2, regdec_1_out_4_3, regdec_1_out_4_4,
       regdec_1_out_4_5, regdec_1_out_4_6, regdec_1_out_4_7, regdec_1_out_4_8, t_ff_1_q;
  wire [2:0] alu_1_out_6, register_1_q;
  wire [3:0] counter_1_q;
  wire [7:0] r0_q, r1_q, r2_q, r3_q, r4_q, r5_2_q, r5_q, r6_q;
  wire [15:0] alu_1_out_5, BP_q, controlled_buffer_3_out, controlled_buffer_11_out, counter_2_q,
       multiplexer_1_out, multiplexer_2_out, pull_resistor_2_node, register_2_q, register_4_q, register_5_q,
       shreg_1_out_3, shreg_2_out_3, SP_q;
  wire [15:8] demultiplexer_1_out0;
  wire [31:0] rom_1_data;

  shreg shreg_1 (.in_1(RAMIn), .in_2(controlled_buffer_11_out[9]), .out_3(shreg_1_out_3));
  not not_1 (not_1_out, ClkIn);
  assign RAMIn = regdec_1_out_4_4[0] ? r3_q : 8'bz;  // Controlled_Buffer controlled_buffer_1
  Register r3 (.D(RAMIn), .Q(r3_q), .clk(regdec_1_out_4_4[1]));  // open: en, clr
  Register r5 (.D(RAMIn), .Q(r5_q), .clk(regdec_1_out_4_8[1]));  // open: en, clr
  assign RAMIn = regdec_1_out_4_8[0] ? r5_q : 8'bz;  // Controlled_Buffer controlled_buffer_2
  Register #(.width(3)) register_1 (
    .D(alu_1_out_6), .Q(register_1_q), .clk(controlled_buffer_11_out[8]));  // open: en, clr
  Register #(.width(16)) register_2 (
    .D(shreg_1_out_3), .Q(register_2_q), .clk(controlled_buffer_11_out[11]));  // open: en, clr
  T_Flip_Flop t_ff_1 (.clk(not_1_out), .T(not_1_out), .Q(t_ff_1_q[0]));  // open: Qn, preset, reset, en
  T_Flip_Flop t_ff_2 (.clk(ClkIn), .T(ClkIn), .Q(t_ff_1_q[1]));  // open: Qn, preset, reset, en
  Register #(.width(16)) BP (
    .D(controlled_buffer_3_out), .Q(BP_q), .clk(controlled_buffer_11_out[6]));  // open: en, clr
  assign controlled_buffer_3_out = pull_resistor_2_node[9] ? BP_q : 16'bz;  // Controlled_Buffer controlled_buffer_3
  Register r2 (.D(RAMIn), .Q(r2_q), .clk(regdec_1_out_4_3[1]));  // open: en, clr
  assign RAMIn = regdec_1_out_4_3[0] ? r2_q : 8'bz;  // Controlled_Buffer controlled_buffer_4
  assign RAMIn = regdec_1_out_4_7[0] ? r6_q : 8'bz;  // Controlled_Buffer controlled_buffer_5
  Register r6 (.D(RAMIn), .Q(r6_q), .clk(regdec_1_out_4_7[1]));  // open: en, clr
  FLG flg_1 (.in_1(register_1_q), .out_3(flg_1_out_3), .cgez(register_2_q[8:6]));
  Counter #(.width(4), .max('hf)) counter_1 (
    .Q(counter_1_q), .clk(decoder_1_out0), .clr(controlled_buffer_11_out[10]));  // open: load, D, count, carry
  Decoder #(.select(2), .disabled(0), .enable("false")) decoder_1 (
    .out0(decoder_1_out0), .out1(decoder_1_out1), .out2(decoder_1_out2), .out3(decoder_1_out3), .sel(t_ff_1_q));
  assign RAMIn = regdec_1_out_4_2[0] ? r1_q : 8'bz;  // Controlled_Buffer controlled_buffer_6
  Register r1 (.D(RAMIn), .Q(r1_q), .clk(regdec_1_out_4_2[1]));  // open: en, clr
  Register r5_2 (.D(RAMIn), .Q(r5_2_q), .clk(regdec_1_out_4_6[1]));  // open: en, clr
  assign RAMIn = regdec_1_out_4_6[0] ? r5_2_q : 8'bz;  // Controlled_Buffer controlled_buffer_7
  or or_1 (or_1_out, decoder_1_out1, decoder_1_out2, decoder_1_out3);
  assign controlled_buffer_3_out = pull_resistor_2_node[8] ? SP_q : 16'bz;  // Controlled_Buffer controlled_buffer_8
  Register #(.width(16)) SP (
    .D(controlled_buffer_3_out), .Q(SP_q), .clk(controlled_buffer_11_out[5]));  // open: en, clr
  Register r0 (.D(RAMIn), .Q(r0_q), .clk(regdec_1_out_4[1]));  // open: en, clr
  assign RAMIn = regdec_1_out_4[0] ? r0_q : 8'bz;  // Controlled_Buffer controlled_buffer_9
  Register r4 (.D(RAMIn), .Q(r4_q), .clk(regdec_1_out_4_5[1]));  // open: en, clr
  assign RAMIn = regdec_1_out_4_5[0] ? r4_q : 8'bz;  // Controlled_Buffer controlled_buffer_10
  ROM #(.addrWidth(12), .dataWidth(32)) rom_1 (
    .addr({flg_1_out_3, register_2_q[15:10], counter_1_q}), .data(rom_1_data));  // open: sel
  regdec regdec_1 (
    .out_4({regdec_1_out_4_8, regdec_1_out_4_7, regdec_1_out_4_6, regdec_1_out_4_5, regdec_1_out_4_4, regdec_1_out_4_3, regdec_1_out_4_2, regdec_1_out_4}),
    .EA_EB(pull_resistor_2_node[11:10]), .EA_EB_2(controlled_buffer_11_out[13:12]), .in_1(register_2_q[5:0]));
  assign {controlled_buffer_11_out[15:8], RAMCtrl[1], controlled_buffer_11_out[6:0]} = decoder_1_out3 ? rom_1_data[15:0] : 16'bz;  // Controlled_Buffer controlled_buffer_11
  Pull_Resistor pull_resistor_1 (.node({controlled_buffer_11_out[15:8], RAMCtrl[1], controlled_buffer_11_out[6:0]}));
  Pull_Resistor pull_resistor_2 (.node({pull_resistor_2_node[15:7], RAMCtrl[0], pull_resistor_2_node[5:0]}));
  assign {pull_resistor_2_node[15:7], RAMCtrl[0], pull_resistor_2_node[5:0]} = or_1_out ? rom_1_data[31:16] : 16'bz;  // Controlled_Buffer controlled_buffer_12
  shreg shreg_2 (.in_1(RAMIn), .in_2(controlled_buffer_11_out[4]), .out_3(shreg_2_out_3));
  // Probe on RAMIn
  Counter #(.width(16), .max('hffff)) counter_2 (
    .load(pull_resistor_2_node[5]), .D(shreg_2_out_3), .count(pull_resistor_2_node[4]), .Q(counter_2_q),
    .clk(controlled_buffer_11_out[3]));  // open: carry, clr
  assign controlled_buffer_3_out = pull_resistor_2_node[3] ? counter_2_q : 16'bz;  // Controlled_Buffer controlled_buffer_13
  // Probe on RAMIn
  Register #(.width(16)) register_3 (
    .D(controlled_buffer_3_out), .Q(RAMOut), .clk(controlled_buffer_11_out[2]));  // open: en, clr
  Multiplexer #(.width(16), .disabled(0), .enable("false")) multiplexer_1 (
    .in0({{8{1'b0}}, RAMIn}), .in1(controlled_buffer_3_out), .out(multiplexer_1_out),
    .sel(pull_resistor_2_node[7]));
  Multiplexer #(.width(16), .disabled(0), .enable("false")) multiplexer_2 (
    .in0({{8{1'b0}}, RAMIn}), .in1(controlled_buffer_3_out), .out(multiplexer_2_out),
    .sel(pull_resistor_2_node[7]));
  ALU alu_1 (
    .A(multiplexer_2_out), .B(register_4_q), .out_6(alu_1_out_6), .in_4(pull_resistor_2_node[2:1]),
    .out_5(alu_1_out_5));  // open: in_3
  // Probe on RAMIn
  Register #(.width(16)) register_4 (
    .D(multiplexer_1_out), .Q(register_4_q), .clk(controlled_buffer_11_out[1]));  // open: en, clr
  Demultiplexer #(.width(16)) demultiplexer_1 (
    .out0({demultiplexer_1_out0, RAMIn}), .out1(controlled_buffer_3_out), .in(register_5_q),
    .sel(pull_resistor_2_node[7]), .en(pull_resistor_2_node[0]));
  Register #(.width(16)) register_5 (
    .D(alu_1_out_5), .Q(register_5_q), .clk(controlled_buffer_11_out[0]));  // open: en, clr
endmodule

module shreg (
  input  [7:0] in_1,
  input  in_2,
  output [15:0] out_3
);

  Register register_1 (.D(in_1), .Q(out_3[7:0]), .clk(in_2));  // open: en, clr
  Register register_2 (.D(out_3[7:0]), .Q(out_3[15:8]), .clk(in_2));  // open: en, clr
endmodule

module regdec (
  input  [5:0] in_1,
  input  [1:0] EA_EB,
  input  [1:0] EA_EB_2,
  output [15:0] out_4
);

  wire [1:0] demultiplexer_1_out0, demultiplexer_1_out1, demultiplexer_1_out2, demultiplexer_1_out3,
       demultiplexer_1_out4, demultiplexer_1_out5, demultiplexer_1_out6, demultiplexer_1_out7,
       demultiplexer_2_out0, demultiplexer_2_out1, demultiplexer_2_out2, demultiplexer_2_out3,
       demultiplexer_2_out4, demultiplexer_2_out5, demultiplexer_2_out6, demultiplexer_2_out7;

  assign out_4[1:0] = demultiplexer_1_out0 | demultiplexer_2_out0;  // OR_Gate or_1, 2 bits wide
  assign out_4[3:2] = demultiplexer_1_out1 | demultiplexer_2_out1;  // OR_Gate or_2, 2 bits wide
  assign out_4[5:4] = demultiplexer_1_out2 | demultiplexer_2_out2;  // OR_Gate or_3, 2 bits wide
  assign out_4[7:6] = demultiplexer_1_out3 | demultiplexer_2_out3;  // OR_Gate or_4, 2 bits wide
  assign out_4[9:8] = demultiplexer_1_out4 | demultiplexer_2_out4;  // OR_Gate or_5, 2 bits wide
  assign out_4[11:10] = demultiplexer_1_out5 | demultiplexer_2_out5;  // OR_Gate or_6, 2 bits wide
  assign out_4[13:12] = demultiplexer_1_out6 | demultiplexer_2_out6;  // OR_Gate or_7, 2 bits wide
  assign out_4[15:14] = demultiplexer_1_out7 | demultiplexer_2_out7;  // OR_Gate or_8, 2 bits wide
  Demultiplexer #(.select(3), .width(2), .disabled(0), .enable("false")) demultiplexer_1 (
    .out0(demultiplexer_1_out0), .out1(demultiplexer_1_out1), .out2(demultiplexer_1_out2),
    .out3(demultiplexer_1_out3), .out4(demultiplexer_1_out4), .out5(demultiplexer_1_out5),
    .out6(demultiplexer_1_out6), .out7(demultiplexer_1_out7), .in({EA_EB[0], EA_EB_2[0]}), .sel(in_1[5:3]));
  Demultiplexer #(.select(3), .width(2), .disabled(0), .enable("false")) demultiplexer_2 (
    .out0(demultiplexer_2_out0), .out1(demultiplexer_2_out1), .out2(demultiplexer_2_out2),
    .out3(demultiplexer_2_out3), .out4(demultiplexer_2_out4), .out5(demultiplexer_2_out5),
    .out6(demultiplexer_2_out6), .out7(demultiplexer_2_out7), .in({EA_EB[1], EA_EB_2[1]}), .sel(in_1[2:0]));
endmodule

module ALU (
  input  [15:0] A,
  input  [15:0] B,
  input  in_3,
  input  [1:0] in_4,
  output [15:0] out_5,
  output [2:0] out_6
);

  wire [15:0] adder_1_out, and_1_out, not_1_out;

  Pull_Resistor pull_resistor_1 (.node(A));
  Pull_Resistor pull_resistor_2 (.node(B));
  Adder #(.width(16)) adder_1 (.a(A), .b(B), .out(adder_1_out), .cin(in_3), .cout(out_6[2]));
  assign and_1_out = A & B;  // AND_Gate and_1, 16 bits wide
  assign not_1_out = ~A;  // NOT_Gate not_1, 16 bits wide
  Comparator #(.width(16)) comparator_1 (.a(A), .b(B), .gt(out_6[1]), .eq(out_6[0]));  // open: lt
  Pull_Resistor pull_resistor_3 (.node(out_6));
  Multiplexer #(.select(2), .width(16), .disabled(0), .enable("false")) multiplexer_1 (
    .in0(adder_1_out), .in1(and_1_out), .in2(not_1_out), .out(out_5), .sel(in_4));  // open: in3
endmodule

module FLG (
  input  [2:0] in_1,
  input  [2:0] cgez,
  output [1:0] out_3
);

  wire undriven;
  wire [2:0] and_1_out;

  // Probe on and_1_out
  assign and_1_out = in_1 & cgez;  // AND_Gate and_1, 3 bits wide
  Priority_Encoder #(.select(2), .disabled(0)) priority_encoder_1 (
    .in0(undriven), .in1(and_1_out[0]), .in2(and_1_out[1]), .in3(and_1_out[2]), .out(out_3));  // open: gs, en_out, en_in
  Pull_Resistor pull_resistor_1 (.node(out_3));
endmodule
