// Logisim project logv2.circ as structural Verilog: 7 circuits, main circuit motherboard
module motherboard (
);

  wire clock_1_out;
  wire [1:0] undriven_2;
  wire [7:0] ram_1_data;
  wire [15:0] undriven;

  Clock clock_1 (.out(clock_1_out));
  // Probe on undriven
  // Probe on ram_1_data
  RAM #(.addrWidth(16)) ram_1 (
    .addr(undriven), .data(ram_1_data), .clk(undriven_2[1]), .ld(undriven_2[0]));  // open: sel, clr
  TTY tty_1 ();  // open: data, clk, we, clr
endmodule

module FLG (
  input  [3:0] in_1,
  input  [1:0] in_2,
  output t_f
);

  wire [3:0] and_1_out, decoder_1_out0;

  Decoder #(.select(2), .disabled(0), .enable("false")) decoder_1 (
    .out0(decoder_1_out0[0]), .out1(decoder_1_out0[1]), .out2(decoder_1_out0[2]), .out3(decoder_1_out0[3]),
    .sel(in_2));
  // Probe on and_1_out
  assign and_1_out = in_1 & decoder_1_out0;  // AND_Gate and_1, 4 bits wide
  or or_1 (t_f, and_1_out[0], and_1_out[1], and_1_out[2], and_1_out[3]);
endmodule

module CPU (
);

  wire clock_1_out, timer_1_r, timer_1_w, undriven, undriven_4, undriven_5, undriven_6, undriven_8,
       undriven_9;
  wire [1:0] register_decoder_1_r0, register_decoder_1_r1, register_decoder_1_r2, register_decoder_1_r3,
       register_decoder_1_r4, register_decoder_1_r5, register_decoder_1_r6, register_decoder_1_r7,
       register_decoder_1_r8x, register_decoder_1_r9x, register_decoder_1_rax, register_decoder_1_rbx,
       undriven_2, undriven_3, undriven_13;
  wire [1:1] undriven_12;
  wire [2:0] undriven_11;
  wire [3:0] alu_1_out_6, register_2_q, timer_1_ct, undriven_7;
  wire [5:1] undriven_10;
  wire [7:0] alu_1_out_5, register_1_q, register_3_q, register_4_q, register_5_q, register_file_1_out_16;
  wire [10:10] flg_1_t_f;
  wire [15:0] counter_1_q, register_file_1_out_15;
  wire [20:0] rom_1_data;

  register_file register_file_1 (
    .in_1(register_file_1_out_15), .out_15(register_file_1_out_15), .in_2(register_file_1_out_16),
    .out_16(register_file_1_out_16), .in_3(register_decoder_1_r0), .in_6(register_decoder_1_r4),
    .in_7(register_decoder_1_rax), .in_8(register_decoder_1_r8x), .in_4(register_decoder_1_r1),
    .in_10(register_decoder_1_r5), .in_11(register_decoder_1_rbx), .in_12(register_decoder_1_r9x),
    .in_5(register_decoder_1_r2), .in_13(register_decoder_1_r6), .in_9(register_decoder_1_r3),
    .in_14(register_decoder_1_r7));
  Register register_1 (.D(register_file_1_out_16), .Q(register_1_q), .clk(undriven));  // open: en, clr
  Clock clock_1 (.out(clock_1_out));
  register_decoder register_decoder_1 (
    .RA(undriven_2), .RB(undriven_3), .R7(register_decoder_1_r7), .R6(register_decoder_1_r6),
    .R5(register_decoder_1_r5), .R4(register_decoder_1_r4), .R3(register_decoder_1_r3),
    .R2(register_decoder_1_r2), .R1(register_decoder_1_r1), .R0(register_decoder_1_r0), .in_3(register_1_q),
    .R8X(register_decoder_1_r8x), .R9X(register_decoder_1_r9x), .RAX(register_decoder_1_rax),
    .RBX(register_decoder_1_rbx));
  Register #(.width(4)) register_2 (.D(alu_1_out_6), .Q(register_2_q), .clk(undriven_4));  // open: en, clr
  Register register_3 (.D(register_file_1_out_16), .Q(register_3_q), .clk(undriven_5));  // open: en, clr
  Timer timer_1 (.rRST(undriven_6), .ct(timer_1_ct), .w(timer_1_w), .r(timer_1_r), .clk(clock_1_out));
  FLG flg_1 (.in_1(register_2_q), .t_f(flg_1_t_f[10]), .in_2(register_3_q[1:0]));
  ROM #(.addrWidth(11), .dataWidth(21)) rom_1 (
    .addr({flg_1_t_f[10], register_3_q[7:2], timer_1_ct}), .data(rom_1_data));  // open: sel
  // Probe on register_file_1_out_15
  // Probe on register_file_1_out_16
  assign register_file_1_out_15 = undriven_7[0] ? counter_1_q : 16'bz;  // Controlled_Buffer controlled_buffer_1
  Counter #(.width(16), .max('hffff), .trigger("falling")) counter_1 (
    .load(undriven_7[3]), .D(register_file_1_out_15), .count(undriven_7[2]), .Q(counter_1_q),
    .clk(undriven_7[1]), .clr(undriven_8));  // open: carry
  // Probe on alu_1_out_6
  Register register_4 (.D(register_file_1_out_16), .Q(register_4_q), .clk(undriven_9));  // open: en, clr
  ALU alu_1 (
    .in_4(undriven_10[5]), .A(register_file_1_out_16), .B(register_4_q), .in_1(undriven_11),
    .out_5(alu_1_out_5), .out_6(alu_1_out_6));
  Register register_5 (.D(alu_1_out_5), .Q(register_5_q), .clk(undriven_12[1]));  // open: en, clr
  assign register_file_1_out_16 = undriven_10[1] ? register_5_q : 8'bz;  // Controlled_Buffer controlled_buffer_2
  RAM #(.addrWidth(16)) ram_1 (
    .addr(register_file_1_out_15), .data(register_file_1_out_16), .clk(undriven_13[1]), .ld(undriven_13[0]));  // open: sel, clr
endmodule

module ALU (
  input  [2:0] in_1,
  input  [7:0] A,
  input  [7:0] B,
  input  in_4,
  output [7:0] out_5,
  output [3:0] out_6
);

  wire adder_1_cout, and_2_out, and_3_out, not_2_out, not_3_out, not_4_out, not_5_out, not_6_out,
       subtractor_1_bout;
  wire [3:0] bitadder_1_out;
  wire [7:0] adder_1_out, and_1_out, not_1_out, or_1_out, subtractor_1_out, undriven, undriven_2, xor_1_out;

  assign not_1_out = ~A;  // NOT_Gate not_1, 8 bits wide
  Adder adder_1 (.a(A), .b(B), .out(adder_1_out), .cin(in_4), .cout(adder_1_cout));
  assign out_6[0] = and_3_out ? adder_1_cout : 1'bz;  // Controlled_Buffer controlled_buffer_1
  Subtractor subtractor_1 (.a(A), .b(B), .out(subtractor_1_out), .bin(in_4), .bout(subtractor_1_bout));
  assign out_6[0] = and_2_out ? subtractor_1_bout : 1'bz;  // Controlled_Buffer controlled_buffer_2
  assign and_1_out = A & B;  // AND_Gate and_1, 8 bits wide
  assign or_1_out = A | B;  // OR_Gate or_1, 8 bits wide
  assign xor_1_out = A ^ B;  // XOR_Gate xor_1, 8 bits wide
  Comparator comparator_1 (.a(A), .b(B), .gt(out_6[1]), .eq(out_6[2]));  // open: lt
  BitAdder bitadder_1 (.in0(A), .out(bitadder_1_out));
  nor nor_1 (out_6[3], bitadder_1_out[0], bitadder_1_out[1], bitadder_1_out[2], bitadder_1_out[3]);
  not not_2 (not_2_out, in_1[1]);
  and and_2 (and_2_out, in_1[0], not_2_out, not_3_out);
  not not_3 (not_3_out, in_1[2]);
  not not_4 (not_4_out, in_1[0]);
  and and_3 (and_3_out, not_4_out, not_5_out, not_6_out);
  not not_5 (not_5_out, in_1[1]);
  not not_6 (not_6_out, in_1[2]);
  Multiplexer #(.select(3), .width(8), .disabled(0), .enable("false")) multiplexer_1 (
    .in0(adder_1_out), .in1(subtractor_1_out), .in2(and_1_out), .in3(or_1_out), .in4(xor_1_out),
    .in5(not_1_out), .in6(undriven), .in7(undriven_2), .out(out_5), .sel(in_1));
endmodule

module register_decoder (
  input  [1:0] RA,
  input  [1:0] RB,
  input  [7:0] in_3,
  output [1:0] R7,
  output [1:0] R6,
  output [1:0] R5,
  output [1:0] R4,
  output [1:0] R3,
  output [1:0] R2,
  output [1:0] R1,
  output [1:0] R0,
  output [1:0] R8X,
  output [1:0] R9X,
  output [1:0] RAX,
  output [1:0] RBX
);

  wire not_1_out, not_2_out;
  wire [1:0] demultiplexer_1_out0, demultiplexer_1_out1, demultiplexer_1_out2, demultiplexer_1_out3,
       demultiplexer_1_out4, demultiplexer_1_out5, demultiplexer_1_out6, demultiplexer_1_out7,
       demultiplexer_2_out0, demultiplexer_2_out1, demultiplexer_2_out2, demultiplexer_2_out3,
       demultiplexer_3_out0, demultiplexer_3_out1, demultiplexer_3_out2, demultiplexer_3_out3,
       demultiplexer_3_out4, demultiplexer_3_out5, demultiplexer_3_out6, demultiplexer_3_out7,
       demultiplexer_4_out0, demultiplexer_4_out1, demultiplexer_4_out2, demultiplexer_4_out3;

  assign R7 = demultiplexer_1_out7 | demultiplexer_3_out7;  // OR_Gate or_1, 2 bits wide
  assign R6 = demultiplexer_1_out6 | demultiplexer_3_out6;  // OR_Gate or_2, 2 bits wide
  assign R5 = demultiplexer_1_out5 | demultiplexer_3_out5;  // OR_Gate or_3, 2 bits wide
  assign R3 = demultiplexer_1_out3 | demultiplexer_3_out3;  // OR_Gate or_4, 2 bits wide
  assign R4 = demultiplexer_1_out4 | demultiplexer_3_out4;  // OR_Gate or_5, 2 bits wide
  assign R0 = demultiplexer_1_out0 | demultiplexer_3_out0;  // OR_Gate or_6, 2 bits wide
  assign R1 = demultiplexer_1_out1 | demultiplexer_3_out1;  // OR_Gate or_7, 2 bits wide
  assign R2 = demultiplexer_1_out2 | demultiplexer_3_out2;  // OR_Gate or_8, 2 bits wide
  Demultiplexer #(.select(3), .width(2), .disabled(0)) demultiplexer_1 (
    .out0(demultiplexer_1_out0), .out1(demultiplexer_1_out1), .out2(demultiplexer_1_out2),
    .out3(demultiplexer_1_out3), .out4(demultiplexer_1_out4), .out5(demultiplexer_1_out5),
    .out6(demultiplexer_1_out6), .out7(demultiplexer_1_out7), .in(RB), .sel(in_3[6:4]), .en(not_1_out));
  not not_1 (not_1_out, in_3[7]);
  Demultiplexer #(.select(2), .width(2), .disabled(0)) demultiplexer_2 (
    .out0(demultiplexer_2_out0), .out1(demultiplexer_2_out1), .out2(demultiplexer_2_out2),
    .out3(demultiplexer_2_out3), .in(RA), .sel(in_3[1:0]), .en(in_3[3]));
  Demultiplexer #(.select(3), .width(2), .disabled(0)) demultiplexer_3 (
    .out0(demultiplexer_3_out0), .out1(demultiplexer_3_out1), .out2(demultiplexer_3_out2),
    .out3(demultiplexer_3_out3), .out4(demultiplexer_3_out4), .out5(demultiplexer_3_out5),
    .out6(demultiplexer_3_out6), .out7(demultiplexer_3_out7), .in(RA), .sel(in_3[2:0]), .en(not_2_out));
  not not_2 (not_2_out, in_3[3]);
  assign R9X = demultiplexer_2_out1 | demultiplexer_4_out1;  // OR_Gate or_9, 2 bits wide
  assign R8X = demultiplexer_2_out0 | demultiplexer_4_out0;  // OR_Gate or_10, 2 bits wide
  Demultiplexer #(.select(2), .width(2), .disabled(0)) demultiplexer_4 (
    .out0(demultiplexer_4_out0), .out1(demultiplexer_4_out1), .out2(demultiplexer_4_out2),
    .out3(demultiplexer_4_out3), .in(RB), .sel(in_3[5:4]), .en(in_3[7]));
  assign RAX = demultiplexer_2_out2 | demultiplexer_4_out2;  // OR_Gate or_11, 2 bits wide
  assign RBX = demultiplexer_2_out3 | demultiplexer_4_out3;  // OR_Gate or_12, 2 bits wide
endmodule

module register_file (
  input  [15:0] in_1,
  input  [7:0] in_2,
  input  [1:0] in_3,
  input  [1:0] in_4,
  input  [1:0] in_5,
  input  [1:0] in_6,
  input  [1:0] in_7,
  input  [1:0] in_8,
  input  [1:0] in_9,
  input  [1:0] in_10,
  input  [1:0] in_11,
  input  [1:0] in_12,
  input  [1:0] in_13,
  input  [1:0] in_14,
  output [15:0] out_15,
  output [7:0] out_16
);

  wire or_1_out, or_2_out, or_3_out, or_4_out;
  wire [7:0] multiplexer_1_out, multiplexer_2_out, multiplexer_3_out, multiplexer_4_out, register_1_q,
       register_2_q, register_3_q, register_4_q, register_5_q, register_6_q, register_7_q, register_8_q;
  wire [15:0] register_9_q, register_10_q;

  assign out_16 = in_9[0] ? register_1_q : 8'bz;  // Controlled_Buffer controlled_buffer_1
  Register register_1 (.D(in_2), .Q(register_1_q), .clk(in_9[1]));  // open: en, clr
  Register register_2 (.D(in_2), .Q(register_2_q), .clk(in_5[1]));  // open: en, clr
  assign out_16 = in_5[0] ? register_2_q : 8'bz;  // Controlled_Buffer controlled_buffer_2
  Register register_3 (.D(in_2), .Q(register_3_q), .clk(in_4[1]));  // open: en, clr
  assign out_16 = in_4[0] ? register_3_q : 8'bz;  // Controlled_Buffer controlled_buffer_3
  Register register_4 (.D(in_2), .Q(register_4_q), .clk(in_3[1]));  // open: en, clr
  assign out_16 = in_3[0] ? register_4_q : 8'bz;  // Controlled_Buffer controlled_buffer_4
  Multiplexer #(.width(8), .disabled(0), .enable("false")) multiplexer_1 (
    .in0(in_2), .in1(in_1[7:0]), .out(multiplexer_1_out), .sel(in_11[1]));
  or or_1 (or_1_out, in_11[1], in_14[1]);
  Multiplexer #(.width(8), .disabled(0), .enable("false")) multiplexer_2 (
    .in0(in_2), .in1(in_1[15:8]), .out(multiplexer_2_out), .sel(in_11[1]));
  or or_2 (or_2_out, in_11[1], in_13[1]);
  Multiplexer #(.width(8), .disabled(0), .enable("false")) multiplexer_3 (
    .in0(in_2), .in1(in_1[7:0]), .out(multiplexer_3_out), .sel(in_7[1]));
  or or_3 (or_3_out, in_7[1], in_10[1]);
  Multiplexer #(.width(8), .disabled(0), .enable("false")) multiplexer_4 (
    .in0(in_2), .in1(in_1[15:8]), .out(multiplexer_4_out), .sel(in_7[1]));
  or or_4 (or_4_out, in_7[1], in_6[1]);
  assign out_16 = in_14[0] ? register_5_q : 8'bz;  // Controlled_Buffer controlled_buffer_5
  Register #(.trigger("falling")) register_5 (
    .D(multiplexer_1_out), .Q(register_5_q), .clk(or_1_out));  // open: en, clr
  Register #(.trigger("falling")) register_6 (
    .D(multiplexer_2_out), .Q(register_6_q), .clk(or_2_out));  // open: en, clr
  assign out_16 = in_13[0] ? register_6_q : 8'bz;  // Controlled_Buffer controlled_buffer_6
  assign out_16 = in_10[0] ? register_7_q : 8'bz;  // Controlled_Buffer controlled_buffer_7
  Register #(.trigger("falling")) register_7 (
    .D(multiplexer_3_out), .Q(register_7_q), .clk(or_3_out));  // open: en, clr
  assign out_15 = in_7[0] ? {register_8_q, register_7_q} : 16'bz;  // Controlled_Buffer controlled_buffer_8
  Register #(.trigger("falling")) register_8 (
    .D(multiplexer_4_out), .Q(register_8_q), .clk(or_4_out));  // open: en, clr
  assign out_16 = in_6[0] ? register_8_q : 8'bz;  // Controlled_Buffer controlled_buffer_9
  assign out_15 = in_11[0] ? {register_6_q, register_5_q} : 16'bz;  // Controlled_Buffer controlled_buffer_10
  assign out_15 = in_8[0] ? register_9_q : 16'bz;  // Controlled_Buffer controlled_buffer_11
  Register #(.width(16)) register_9 (.D(in_1), .Q(register_9_q), .clk(in_8[1]));  // open: en, clr
  assign out_15 = in_12[0] ? register_10_q : 16'bz;  // Controlled_Buffer controlled_buffer_12
  Register #(.width(16)) register_10 (.D(in_1), .Q(register_10_q), .clk(in_12[1]));  // open: en, clr
endmodule

module Timer (
  input  rRST,
  input  clk,
  output [3:0] ct,
  output w,
  output r
);

  wire and_1_out, decoder_1_out0, decoder_1_out1, decoder_1_out2, not_1_out, t_ff_1_q;
  wire [1:0] t_ff_2_q;

  not not_1 (not_1_out, clk);
  T_Flip_Flop t_ff_1 (.clk(rRST), .T(rRST), .Q(t_ff_1_q), .reset(decoder_1_out0));  // open: Qn, preset, en
  T_Flip_Flop t_ff_2 (.clk(not_1_out), .T(not_1_out), .Q(t_ff_2_q[0]));  // open: Qn, preset, reset, en
  T_Flip_Flop t_ff_3 (.clk(clk), .T(clk), .Q(t_ff_2_q[1]));  // open: Qn, preset, reset, en
  and and_1 (and_1_out, t_ff_1_q, decoder_1_out0);
  Decoder #(.select(2), .disabled(0), .enable("false")) decoder_1 (
    .out0(decoder_1_out0), .out1(decoder_1_out1), .out2(decoder_1_out2), .out3(r), .sel(t_ff_2_q));
  Counter #(.width(4), .max('hf)) counter_1 (
    .Q(ct), .clk(decoder_1_out0), .clr(and_1_out));  // open: load, D, count, carry
  or or_1 (w, decoder_1_out1, decoder_1_out2, r);
endmodule
